// Logisim project additionner_syslog.circ as structural Verilog
module bit_counter (
  input  In3,
  input  In4
);

  wire [1:0] clock_1_out;

  Clock clock_1 (.out(clock_1_out[0]));
  Clock clock_2 (.out(clock_1_out[1]));
  Hex_Digit_Display hex_digit_display_1 (.value({In4, In3, clock_1_out}));  // open: dp
endmodule

module one_digit_display (
  input  input_1
);

  wire clock_1_out;
  wire [3:0] additionner_0_9_1_one;

  Clock clock_1 (.out(clock_1_out));
  additionner_0_9 additionner_0_9_1 (
    .in_1(input_1), .CLK_input(clock_1_out), .one(additionner_0_9_1_one[0]), .two(additionner_0_9_1_one[1]),
    .four(additionner_0_9_1_one[2]), .eight(additionner_0_9_1_one[3]));
  Hex_Digit_Display hex_digit_display_1 (.value(additionner_0_9_1_one));  // open: dp
endmodule

module divide_by_2 (
  input  clock_input,
  output ou1
);

  wire d_ff_1_q, d_ff_1_qn;

  D_Flip_Flop d_ff_1 (.D(d_ff_1_qn), .clk(clock_input), .Q(d_ff_1_q), .Qn(d_ff_1_qn));  // open: preset, reset
  not not_1 (ou1, d_ff_1_q);
endmodule

module divide_by_4 (
  input  clock_input,
  output ou2
);

  wire d_ff_1_q, d_ff_1_qn, d_ff_2_qn;

  D_Flip_Flop d_ff_1 (.D(d_ff_1_qn), .clk(clock_input), .Q(d_ff_1_q), .Qn(d_ff_1_qn));  // open: preset, reset
  D_Flip_Flop d_ff_2 (.D(d_ff_2_qn), .clk(d_ff_1_q), .Q(ou2), .Qn(d_ff_2_qn));  // open: preset, reset
endmodule

module divide_by_8 (
  input  clock_input,
  output ou3
);

  wire d_ff_1_q, d_ff_1_qn, d_ff_2_q, d_ff_2_qn, d_ff_3_q, d_ff_3_qn;

  D_Flip_Flop d_ff_1 (.D(d_ff_1_qn), .clk(clock_input), .Q(d_ff_1_q), .Qn(d_ff_1_qn));  // open: preset, reset
  D_Flip_Flop d_ff_2 (.D(d_ff_2_qn), .clk(d_ff_1_q), .Q(d_ff_2_q), .Qn(d_ff_2_qn));  // open: preset, reset
  D_Flip_Flop d_ff_3 (.D(d_ff_3_qn), .clk(d_ff_2_q), .Q(d_ff_3_q), .Qn(d_ff_3_qn));  // open: preset, reset
  not not_1 (ou3, d_ff_3_q);
endmodule

module additionner_0_9 (
  input  in_1,
  input  CLK_input,
  output one,
  output two,
  output four,
  output eight
);

  wire and_1_out, j_k_ff_1_q, j_k_ff_2_q, j_k_ff_3_q, not_1_out, undriven;

  J_K_Flip_Flop j_k_ff_1 (
    .J(in_1), .K(in_1), .clk(CLK_input), .Q(j_k_ff_1_q), .Qn(one), .preset(and_1_out));  // open: reset
  J_K_Flip_Flop j_k_ff_2 (
    .J(in_1), .K(in_1), .clk(j_k_ff_1_q), .Q(j_k_ff_2_q), .Qn(two), .preset(and_1_out), .reset(undriven));
  J_K_Flip_Flop j_k_ff_3 (
    .J(in_1), .K(in_1), .clk(j_k_ff_2_q), .Q(j_k_ff_3_q), .Qn(four), .preset(and_1_out));  // open: reset
  not not_1 (not_1_out, j_k_ff_2_q);
  J_K_Flip_Flop j_k_ff_4 (.J(in_1), .K(in_1), .clk(j_k_ff_3_q), .Qn(eight), .preset(and_1_out));  // open: Q, reset
  and and_1 (and_1_out, not_1_out, eight);
endmodule
