// Logisim project time.circ as structural Verilog: 6 circuits, main circuit seconds_counter
module seconds_counter (
  input  run_wk_s,
  input  CLK_input,
  input  run_st_s,
  input  set_mode,
  output [3:0] s1_output,
  output s_c_out,
  output [3:0] s2_output
);

  wire and_1_out, and_3_out, and_5_out, not_1_out, or_1_out, out_1, out_2;

  not not_1 (not_1_out, set_mode);
  or or_1 (or_1_out, run_st_s, and_1_out);
  and and_1 (and_1_out, out_1, not_1_out);
  and and_2 (out_1, s1_output[0], s1_output[3]);
  and and_3 (and_3_out, s1_output[1], s1_output[3]);
  add_4_bits add_4_bits_1 (.enable(run_wk_s), .CLK_input(CLK_input), .Reset(and_3_out), .out_put(s1_output));
  and and_4 (s_c_out, out_1, and_5_out);
  add_4_bits add_4_bits_2 (.enable(or_1_out), .CLK_input(CLK_input), .Reset(out_2), .out_put(s2_output));
  and and_5 (and_5_out, s2_output[0], s2_output[2]);
  and and_6 (out_2, s2_output[1], s2_output[2]);

  // Other names for the same wires on the sheet: c_out = s_c_out
endmodule

module date (
  input  set_mode,
  input  next_digit,
  output nv_jour
);

  wire and_1_out, and_2_out, and_3_out, and_4_out, and_5_out, and_6_out, and_7_out, but_in_out, clock_1_out,
       demultiplexer_1_out0, demultiplexer_1_out1, demultiplexer_1_out2, demultiplexer_1_out3,
       demultiplexer_1_out4, demultiplexer_1_out5, demultiplexer_1_out6, minutes_counter_1_c_out, not_1_out,
       not_2_out, or_1_out, seconds_counter_1_s_c_out;
  wire [2:0] add_4_bits_1_out_put;
  wire [3:0] hours_counter_1_st_hr, hours_counter_1_wk_hr, minutes_counter_1_m1_out,
       minutes_counter_1_m2_out, multiplexer_1_out, multiplexer_2_out, multiplexer_3_out, multiplexer_4_out,
       multiplexer_5_out, multiplexer_6_out, seconds_counter_1_s1_output, seconds_counter_1_s2_output;
  wire [3:3] add_4_bits_1_out_put_2;

  not not_1 (not_1_out, demultiplexer_1_out6);
  Demultiplexer #(.select(3), .enable("false")) demultiplexer_1 (
    .out0(demultiplexer_1_out0), .out1(demultiplexer_1_out1), .out2(demultiplexer_1_out2),
    .out3(demultiplexer_1_out3), .out4(demultiplexer_1_out4), .out5(demultiplexer_1_out5),
    .out6(demultiplexer_1_out6), .in(next_digit), .sel(add_4_bits_1_out_put));  // open: out7
  Button but_in (.out(but_in_out));
  Clock clock_1 (.out(clock_1_out));
  and and_1 (and_1_out, set_mode, but_in_out, demultiplexer_1_out0);
  add_4_bits add_4_bits_1 (
    .enable(not_1_out), .CLK_input(next_digit), .Reset(demultiplexer_1_out6),
    .out_put({add_4_bits_1_out_put_2[3], add_4_bits_1_out_put}));
  not not_2 (not_2_out, set_mode);
  or or_1 (or_1_out, not_2_out, and_1_out);
  and and_2 (and_2_out, set_mode, but_in_out, demultiplexer_1_out1);
  and and_3 (and_3_out, set_mode, but_in_out, demultiplexer_1_out2);
  and and_4 (and_4_out, set_mode, but_in_out, demultiplexer_1_out3);
  and and_5 (and_5_out, set_mode, but_in_out, demultiplexer_1_out4);
  and and_6 (and_6_out, set_mode, but_in_out, demultiplexer_1_out5);
  and and_7 (and_7_out, clock_1_out, set_mode);
  seconds_counter seconds_counter_1 (
    .run_wk_s(or_1_out), .CLK_input(clock_1_out), .run_st_s(and_2_out), .set_mode(set_mode),
    .s1_output(seconds_counter_1_s1_output), .s_c_out(seconds_counter_1_s_c_out),
    .s2_output(seconds_counter_1_s2_output));
  minutes_counter minutes_counter_1 (
    .run_wk_mn(and_3_out), .c_in(seconds_counter_1_s_c_out), .CLK_input(clock_1_out), .run_st_mn(and_4_out),
    .m1_out(minutes_counter_1_m1_out), .m2_out(minutes_counter_1_m2_out), .c_out(minutes_counter_1_c_out));
  hours_counter hours_counter_1 (
    .run_st_hr(and_6_out), .run_wk_hr(and_5_out), .CLK_input(clock_1_out), .c_in_m(minutes_counter_1_c_out),
    .c_in_s(seconds_counter_1_s_c_out), .set_mode(set_mode), .c_out(nv_jour), .st_hr(hours_counter_1_st_hr),
    .wk_hr(hours_counter_1_wk_hr));
  Hex_Digit_Display hex_digit_display_1 (.value(multiplexer_2_out));  // open: dp
  Hex_Digit_Display hex_digit_display_2 (.value(multiplexer_1_out));  // open: dp
  Multiplexer #(.width(4), .enable("false")) multiplexer_1 (
    .in1(hours_counter_1_st_hr), .out(multiplexer_1_out), .sel(1'b1));  // open: in0
  Multiplexer #(.width(4), .enable("false")) multiplexer_2 (
    .in1(hours_counter_1_wk_hr), .out(multiplexer_2_out), .sel(1'b1));  // open: in0
  Hex_Digit_Display hex_digit_display_3 (.value(multiplexer_3_out));  // open: dp
  Multiplexer #(.width(4), .enable("false")) multiplexer_3 (
    .in1(minutes_counter_1_m2_out), .out(multiplexer_3_out), .sel(1'b1));  // open: in0
  Hex_Digit_Display hex_digit_display_4 (.value(multiplexer_4_out));  // open: dp
  Multiplexer #(.width(4), .enable("false")) multiplexer_4 (
    .in1(minutes_counter_1_m1_out), .out(multiplexer_4_out), .sel(1'b1));  // open: in0
  Hex_Digit_Display hex_digit_display_5 (.value(multiplexer_5_out));  // open: dp
  Multiplexer #(.width(4), .enable("false")) multiplexer_5 (
    .in1(seconds_counter_1_s2_output), .out(multiplexer_5_out), .sel(1'b1));  // open: in0
  Hex_Digit_Display hex_digit_display_6 (.value(multiplexer_6_out));  // open: dp
  Multiplexer #(.width(4), .enable("false")) multiplexer_6 (
    .in1(seconds_counter_1_s1_output), .out(multiplexer_6_out), .sel(1'b1));  // open: in0

  // Notes on the sheet:
  //   fix 29 in set mode
endmodule

module minutes_counter (
  input  run_wk_mn,
  input  c_in,
  input  CLK_input,
  input  run_st_mn,
  output [3:0] m1_out,
  output [3:0] m2_out,
  output c_out
);

  wire and_1_out, and_4_out, and_5_out, or_1_out, or_2_out, out_4, out_5;

  and and_1 (and_1_out, c_in, out_4);
  or or_1 (or_1_out, run_wk_mn, c_in);
  or or_2 (or_2_out, run_st_mn, and_1_out);
  and and_2 (c_out, out_4, and_5_out);
  and and_3 (out_4, m1_out[3], m1_out[0]);
  and and_4 (and_4_out, m1_out[3], m1_out[1]);
  add_4_bits add_4_bits_1 (.enable(or_1_out), .CLK_input(CLK_input), .Reset(and_4_out), .out_put(m1_out));
  and and_5 (and_5_out, m2_out[0], m2_out[2]);
  add_4_bits add_4_bits_2 (.enable(or_2_out), .CLK_input(CLK_input), .Reset(out_5), .out_put(m2_out));
  and and_6 (out_5, m2_out[2], m2_out[1]);

  // Notes on the sheet:
  //   is c_in alright ?
endmodule

module hours_counter (
  input  run_st_hr,
  input  run_wk_hr,
  input  CLK_input,
  input  c_in_m,
  input  c_in_s,
  input  set_mode,
  output c_out,
  output [3:0] st_hr,
  output [3:0] wk_hr
);

  wire and_1_out, and_2_out, and_4_out, and_5_out, and_6_out, incr_1, incr_2, not_1_out, or_1_out, or_2_out,
       or_3_out, or_4_out, out_6, out_7;

  not not_1 (not_1_out, set_mode);
  and and_1 (and_1_out, and_2_out, incr_2);
  and and_2 (and_2_out, c_in_m, c_in_s, not_1_out);
  or or_1 (or_1_out, c_out, out_7);
  or or_2 (or_2_out, run_st_hr, and_1_out);
  or or_3 (or_3_out, c_out, out_6);
  or or_4 (or_4_out, run_wk_hr, and_2_out);
  add_4_bits add_4_bits_1 (.enable(or_2_out), .CLK_input(CLK_input), .Reset(or_1_out), .out_put(st_hr));
  add_4_bits add_4_bits_2 (.enable(or_4_out), .CLK_input(CLK_input), .Reset(or_3_out), .out_put(wk_hr));
  or or_5 (c_out, and_4_out, and_5_out, and_6_out);
  and and_3 (out_7, st_hr[0], st_hr[1]);
  and and_4 (and_4_out, wk_hr[2], st_hr[1]);
  and and_5 (and_5_out, st_hr[1], st_hr[0], wk_hr[3]);
  and and_6 (and_6_out, st_hr[1], wk_hr[0], wk_hr[2]);
  and and_7 (out_6, wk_hr[1], wk_hr[3]);
  and and_8 (incr_1, wk_hr[3], wk_hr[1]);
  and and_9 (incr_2, wk_hr[0], wk_hr[3]);

  // Other names for the same wires on the sheet: reset = c_out
endmodule

module dmy (
  input  in_1
);

  wire button_1_out, CLK_input, counter_1_carry, date_1_nv_jour;
  wire [3:0] counter_2_q;

  Clock clock_1 (.out(CLK_input));
  Button button_1 (.out(button_1_out));
  date date_1 (.set_mode(in_1), .next_digit(CLK_input), .nv_jour(date_1_nv_jour));
  Counter #(.width(5), .max('h1f)) counter_1 (
    .clk(date_1_nv_jour), .carry(counter_1_carry));  // open: clr, load, up, count, D, Q
  Counter #(.width(4), .max('h1)) counter_2 (
    .clk(counter_1_carry), .Q(counter_2_q));  // open: clr, load, up, count, D, carry
  D_Flip_Flop d_ff_1 (.D(counter_1_carry), .clk(CLK_input));  // open: Q, Qn, preset, reset
endmodule

module add_4_bits (
  input  enable,
  input  CLK_input,
  input  Reset,
  output [3:0] out_put
);

  wire and_1_out, and_2_out, and_3_out, and_4_out, and_5_out;

  J_K_Flip_Flop j_k_ff_1 (.J(enable), .K(enable), .clk(CLK_input), .Q(out_put[0]), .reset(Reset));  // open: Qn, preset
  J_K_Flip_Flop j_k_ff_2 (
    .J(and_1_out), .K(and_1_out), .clk(CLK_input), .Q(out_put[1]), .reset(Reset));  // open: Qn, preset
  and and_1 (and_1_out, enable, out_put[0]);
  and and_2 (and_2_out, out_put[1], out_put[0]);
  and and_3 (and_3_out, enable, and_2_out);
  J_K_Flip_Flop j_k_ff_3 (
    .J(and_3_out), .K(and_3_out), .clk(CLK_input), .Q(out_put[2]), .reset(Reset));  // open: Qn, preset
  and and_4 (and_4_out, and_2_out, out_put[2]);
  J_K_Flip_Flop j_k_ff_4 (
    .J(and_5_out), .K(and_5_out), .clk(CLK_input), .Q(out_put[3]), .reset(Reset));  // open: Qn, preset
  and and_5 (and_5_out, enable, and_4_out);

  // Other names for the same wires on the sheet: EN = enable
endmodule
